// Logisim project bussim.circ as structural Verilog: 1 circuit, main circuit main
module main (
);

  wire controlled_buffer_1_out, CS012_sw1, CS012_sw2, CS012_sw3, d_ff_1_qn, d_ff_2_qn, d_ff_3_qn, d_ff_4_q,
       d_ff_4_qn, DC_out, DIP_sw1, DIP_sw2, DIP_sw3, nand_1_out, RST_out, SYN_out, xor_1_out, xor_2_out,
       xor_3_out, xor_4_out;

  Button #(.press("passive")) RST (.out(RST_out));
  xor xor_1 (xor_1_out, 1'b1, RST_out);
  DipSwitch #(.number(3)) DIP (.sw1(DIP_sw1), .sw2(DIP_sw2), .sw3(DIP_sw3));
  D_Flip_Flop d_ff_1 (.D(DIP_sw1), .clk(xor_1_out), .Qn(d_ff_1_qn), .preset(1'b0), .reset(1'b0));  // open: Q
  D_Flip_Flop d_ff_2 (.D(DIP_sw2), .clk(xor_1_out), .Qn(d_ff_2_qn), .preset(1'b0), .reset(1'b0));  // open: Q
  D_Flip_Flop d_ff_3 (.D(DIP_sw3), .clk(xor_1_out), .Qn(d_ff_3_qn), .preset(1'b0), .reset(1'b0));  // open: Q
  DipSwitch #(.number(3)) CS012 (.sw1(CS012_sw1), .sw2(CS012_sw2), .sw3(CS012_sw3));
  xor xor_2 (xor_2_out, d_ff_1_qn, CS012_sw1);
  xor xor_3 (xor_3_out, d_ff_2_qn, CS012_sw2);
  xor xor_4 (xor_4_out, d_ff_3_qn, CS012_sw3);
  nand nand_1 (nand_1_out, xor_2_out, xor_3_out, xor_4_out);
  Button SYN (.out(SYN_out));
  Button DC (.out(DC_out));
  D_Flip_Flop d_ff_4 (.D(nand_1_out), .clk(SYN_out), .Q(d_ff_4_q), .Qn(d_ff_4_qn), .preset(1'b0), .reset(1'b0));
  LED #(.active("false")) led_1 (.in(d_ff_4_q));
  assign controlled_buffer_1_out = d_ff_4_qn ? DC_out : 1'bz;  // Controlled_Buffer controlled_buffer_1
endmodule
